# Fritzing sketch sketch A32U4 relai psu atx (saved by Fritzing 0.9.4)
breadboards: 1

parts:
  U1 = RELAY [package=relay-jzc]
  S1 = Round Pushbutton
  J1 = ATX24 Pin Power Supply Connector [package=atx24_right_angle]
  Part1 = Arduino Micro (Rev3)

nets:
  N1: U1.COIL2, Part1.5V
  N2: U1.NC, J1.PWR_OK
  N3: U1.NO, Part1.D10_PWM/A10
  N4: U1.MAIN, J1.5V_STDBY
  N5: S1.leg0, Part1.A3
  N6: S1.leg1, Part1.GND
